# Fritzing sketch RFID-password-generator (saved by Fritzing 0.9.3b)
circuit board: 2.28cm x 3.06cm
stripboards: 1

parts:
  RC522 = female pin header, 8 pins [form="♀ (female)"]
  ATtiny84 = IC, DIP package, 14 pins [chip_label=IC]
  12_MHz = Crystal [frequency="16 Mhz" package=THT]
  3_6V = Rectifier Diode [breakdown_voltage=3.6V package="Melf DO-213 AA [SMD]"]
  R3 = Resistor [tolerance=±1% resistance=68 package="1206 [SMD]"]
  3_6V_2 = Rectifier Diode [breakdown_voltage=3.6V package="Melf DO-213 AA [SMD]"]
  R1 = Resistor [tolerance=±1% resistance=68 package="1206 [SMD]"]
  R5 = Resistor [tolerance=±1% resistance=2.2k package="1206 [SMD]"]
  C1 = Ceramic Capacitor [capacitance=22pF package="1206 [SMD, multilayer]"]
  C2 = Ceramic Capacitor [capacitance=22pF package="1206 [SMD, multilayer]"]
  C3 = Ceramic Capacitor [capacitance=10µF package="1206 [SMD, multilayer]"]
  3_3V = Voltage Regulator [package=to-92]
  USB = USB-Stecker
  S3 = Pushbutton [package="[THT]"]

nets:
  N1: RC522.pin1, C3.1, 3_3V.GND
  N2: RC522.pin3, ATtiny84.pin14, 3_6V.anode, 3_6V_2.anode, C1.0, C2.1, C3.0, 3_3V.IN, USB.GND, S3.Pin_1, S3.Pin_2
  N3: RC522.pin5, ATtiny84.pin7
  N4: RC522.pin6, ATtiny84.pin8
  N5: RC522.pin7, ATtiny84.pin9
  N6: RC522.pin8, ATtiny84.pin13
  N7: ATtiny84.pin1, 3_3V.OUT, USB.VCC
  N8: ATtiny84.pin2, 12_MHz.pin_1, C1.1
  N9: ATtiny84.pin3, 12_MHz.pin_0, C2.0
  N10: ATtiny84.pin5, 3_6V_2.cathode, R1.Pin_1, USB.D+
  N11: ATtiny84.pin6, R5.Pin_1
  N12: ATtiny84.pin10, S3.Pin_3, S3.Pin_4
  N13: ATtiny84.pin11, R3.Pin_0
  N14: ATtiny84.pin12, R1.Pin_0
  N15: 3_6V.cathode, R3.Pin_1, R5.Pin_0, USB.D-

custom parts:
  USB-Stecker: USB-Stecker für Platinen
